# Fritzing sketch sunduino (saved by Fritzing 0.9.1b)
breadboards: 1

parts:
  R1 = Resistor [tolerance=±5% resistance=10k package=THT]
  R2 = Resistor [tolerance=±5% resistance=10k package=THT]
  R3 = Photocell (LDR) [package=THT]
  Part1 = Arduino Uno (Rev3)
  Raspberry_Pi_B_rev1 = Raspberry Pi B rev2
  RHT1 = Humidity and Temperature Sensor RHT03
  R4 = Resistor [tolerance=±5% resistance=1k package=THT]
  R5 = Resistor [tolerance=±5% resistance=1k package=THT]
  U1 = VCNL4000 [package=vcnl4000]
  Adafruit_Atmega32u1 = Adafruit Atmega32u4 Breakout Board [part_number="Atmega 32u4"]  # not connected
  part = Resistor [tolerance=±5% resistance=220 package=THT]  # not connected

nets:
  N1: R1.Pin_0, R3.pin_0, Part1.A0
  GND: R1.Pin_1, Part1.GND, Raspberry_Pi_B_rev1.GND, RHT1.GND_2, R5.Pin_1, U1.IR-
  5V: R2.Pin_0, R3.pin_1, Part1.5V, RHT1.Vcc
  N2: R2.Pin_1, Part1.D2, RHT1.Data-signal
  N3: Part1.A4/SDA, U1.SCL
  N4: Part1.A5/SCL, U1.GND
  N5: Part1.D0/RX, Raspberry_Pi_B_rev1.GPIO_14
  N6: Part1.D1/TX, R4.Pin_1
  N7: Part1.3V3, U1.IR+
  N8: Raspberry_Pi_B_rev1.GPIO_15, R4.Pin_0, R5.Pin_0

notes:
  serial
  Ignore placeholder pcb for TSL 2561
  Pins: Vin, GND, 3vo, Addr, Int, ADA, SCL
