# Fritzing sketch sunduino (saved by Fritzing 0.8.5b)
breadboards: 1
perfboards: 1

parts:
  R1 = Resistor [tolerance=±5% resistance=10k package=THT]
  R2 = Resistor [tolerance=±5% resistance=10k package=THT]
  R3 = Photocell (LDR) [package=THT]
  Part1 = Arduino Uno (Rev3)
  Raspberry_Pi_B_rev1 = Raspberry Pi B rev2
  RHT1 = Humidity and Temperature Sensor RHT03
  R4 = Resistor [tolerance=±5% resistance=1k package=THT]
  R5 = Resistor [tolerance=±5% resistance=1k package=THT]

nets:
  N1: R1.Pin_0, R3.pin_0, Part1.A0
  GND: R1.Pin_1, Part1.GND, Raspberry_Pi_B_rev1.GND, RHT1.GND_2, R5.Pin_1
  5V: R2.Pin_0, R3.pin_1, Part1.5V, RHT1.Vcc
  N2: R2.Pin_1, Part1.D2, RHT1.Data-signal
  N3: Part1.D0/RX, Raspberry_Pi_B_rev1.GPIO_14
  N4: Part1.D1/TX, R4.Pin_1
  N5: Raspberry_Pi_B_rev1.GPIO_15, R4.Pin_0, R5.Pin_0

notes:
  serial
  Vin GND 3vo Addr Int ADA SCL
